# Fritzing sketch zapojeni (saved by Fritzing 0.9.3b)
circuit board: 3.32013cm x 6.65133cm

parts:
  Součástka1 = Arduino Nano (Rev3.0)
  H-most = FTDI_BASIC [package=ftdi_basic]
  Cam_Servo = Basic Servo
  RasPi_killswitch = Momentary Switch [package=tactile-pth]
  záložní_servo = Basic Servo
  RasPi_GPIO = mystery part, 2 pins [chip_label="Raspi GPIO"]
  H_most_out_5V = mystery part, 2 pins [chip_label="Raspi GPIO"]
  lista = mystery part, 15 pins [chip_label=??]
  Lišta = mystery part, 4 pins [chip_label=???]
  POdsvícení = mystery part, 2 pins [chip_label=LEDS]
  +5V_HUB = mystery part, 5 pins [chip_label=+5V]
  GND_HUB = mystery part, 5 pins [chip_label=GND]
  R2 = Resistor [tolerance=±5% resistance=220 package=THT]
  R3 = Resistor [tolerance=±5% resistance=220 package=THT]

nets:
  N1: Součástka1.D1/TX, Lišta.pin4
  N2: Součástka1.D0/RX, Lišta.pin3
  N3: Součástka1.RESET, lista.pin3, Lišta.pin2
  GND: Součástka1.GND, Cam_Servo.gnd, záložní_servo.gnd, H_most_out_5V.pin2, lista.pin2, GND_HUB.pin1, GND_HUB.pin2, GND_HUB.pin3, GND_HUB.pin4, GND_HUB.pin5
  N4: Součástka1.D2, Lišta.pin1
  N5: Součástka1.D3, H-most.6
  N6: Součástka1.D4, H-most.5
  N7: Součástka1.D5, H-most.4
  N8: Součástka1.D6, H-most.3
  N9: Součástka1.D7, H-most.2
  N10: Součástka1.D8, Cam_Servo.pulse
  N11: Součástka1.D9, záložní_servo.pulse
  N12: Součástka1.D10, R2.Pin_0
  N13: Součástka1.D11/MOSI, H-most.1
  N14: Součástka1.D12/MISO, R3.Pin_0
  N15: Součástka1.VIN, lista.pin1
  N16: Součástka1.5V, lista.pin4
  N17: Součástka1.A7, lista.pin5
  N18: Součástka1.A6, lista.pin6
  N19: Součástka1.A5, lista.pin7
  N20: Součástka1.A4, lista.pin8
  N21: Součástka1.A3, lista.pin9
  N22: Součástka1.A2, lista.pin10
  N23: Součástka1.A1, lista.pin11
  N24: Součástka1.A0, lista.pin12
  N25: Součástka1.AREF, lista.pin13
  N26: Součástka1.3V3, lista.pin14
  N27: Součástka1.D13/SCK, lista.pin15
  VCC: Cam_Servo.vcc, záložní_servo.vcc, H_most_out_5V.pin1, +5V_HUB.pin1, +5V_HUB.pin2, +5V_HUB.pin3, +5V_HUB.pin4, +5V_HUB.pin5
  N28: RasPi_killswitch.1, RasPi_GPIO.pin2
  N29: RasPi_killswitch.3, RasPi_GPIO.pin1
  N30: POdsvícení.pin1, R3.Pin_1
  N31: POdsvícení.pin2, R2.Pin_1
